# Fritzing sketch Schaltplan (saved by Fritzing 0.9.3b)
breadboards: 1

parts:
  Launchpad1 = TI Launchpad TM4C123GXL
  Q1 = LTR-301 [package=ltr-301]
  R1 = Resistor [tolerance=±5% resistance=100k package="2010 [SMD]"]
  C1 = Electrolytic Capacitor [capacitance=100µF voltage=10V package="200 mil [THT, electrolytic]"]
  R2 = Resistor [tolerance=±5% resistance=100k package="2010 [SMD]"]
  R4 = Resistor [tolerance=±5% resistance=150 package="2010 [SMD]"]
  LED1 = smd LED [color="Red (633nm)" package="0805 [SMD]"]

nets:
  N1: Launchpad1.PD0, C1.+, R2.Pin_0
  N2: Launchpad1.PD1, Q1.C, R1.Pin_0
  N3: Launchpad1.PC4, R2.Pin_1, R4.Pin_0
  N4: Launchpad1.3.3V, Q1.E
  N5: Launchpad1.GND, R1.Pin_1, C1.-, LED1.cathode
  N6: R4.Pin_1, LED1.anode
